// Logisim project LookAhead.circ as structural Verilog
module Full_Adder (
  input  A,
  input  B,
  input  C_in,
  output Prop,
  output Soma,
  output Gen
);

  xor xor_1 (Prop, A, B);
  and and_1 (Gen, A, B);
  xor xor_2 (Soma, Prop, C_in);
endmodule

module module_lk (
  input  C_in,
  input  [3:0] A,
  input  [3:0] B,
  output G_G,
  output P_G
);

  wire and_1_out, and_2_out, and_3_out, full_adder_1_gen, full_adder_1_prop, full_adder_2_gen,
       full_adder_2_prop, or_1_out, or_2_out;

  Full_Adder full_adder_1 (
    .A(A[0]), .B(B[0]), .C_in(C_in), .Prop(full_adder_1_prop), .Gen(full_adder_1_gen));  // open: Soma
  Full_Adder full_adder_2 (
    .A(A[1]), .B(B[1]), .C_in(or_1_out), .Prop(full_adder_2_prop), .Gen(full_adder_2_gen));  // open: Soma
  Full_Adder full_adder_3 (.A(A[3]), .B(B[3]));  // open: C_in, Prop, Soma, Gen
  and and_1 (and_1_out, C_in, full_adder_1_prop);
  Full_Adder full_adder_4 (.A(A[2]), .B(B[2]), .C_in(or_2_out));  // open: Prop, Soma, Gen
  or or_1 (or_1_out, and_1_out, full_adder_1_gen);
  and and_2 (and_2_out, full_adder_1_gen, full_adder_2_prop);
  and and_3 (and_3_out, full_adder_1_prop, full_adder_2_prop, C_in);
  or or_2 (or_2_out, and_2_out, full_adder_2_gen, and_3_out);
  // OR_Gate or_3 is placed but not wired
endmodule
