// Logisim project ATIVIDADE_CONTADORES.circ as structural Verilog: 2 circuits, main circuit main
module main (
  output [2:0] SAIDA
);

  wire Botao_iniciar_em_4_out, Clear_out, CLK_out;

  Button Botao_iniciar_em_4 (.out(Botao_iniciar_em_4_out));
  Clock CLK (.out(CLK_out));
  Button Clear (.out(Clear_out));
  Circuito_interno circuito_interno_1 (
    .Iniciar_em_4(Botao_iniciar_em_4_out), .CLK(CLK_out), .Clear(Clear_out), .Saida(SAIDA));
  LED led_1 (.in(SAIDA[2]));
  LED led_2 (.in(SAIDA[1]));
  LED led_3 (.in(SAIDA[0]));

  // Notes on the sheet:
  //   como nunca iniciara em 4
  //   este botão serve para isso
  //   ATIVIDADE CONTADOR SINCRONO
endmodule

module Circuito_interno (
  input  Iniciar_em_4,
  input  CLK,
  input  Clear,
  output [2:0] Saida
);

  wire and_1_out, JQ1_out, JQ2_out, KQ1_out, or_1_out, or_2_out, or_3_out;

  xor JQ2 (JQ2_out, Saida[1], Saida[0]);
  J_K_Flip_Flop FKJ2 (
    .J(JQ2_out), .K(Saida[0]), .clk(CLK), .Q(Saida[2]), .preset(Iniciar_em_4), .reset(Clear));  // open: Qn
  or JQ1 (JQ1_out, ~Saida[0], Saida[2]);  // OR_Gate
  and KQ1 (KQ1_out, Saida[2], Saida[0]);
  J_K_Flip_Flop FJK1 (.J(JQ1_out), .K(KQ1_out), .clk(CLK), .Q(Saida[1]), .reset(or_1_out));  // open: Qn, preset
  or or_1 (or_1_out, Clear, Iniciar_em_4);
  or or_2 (or_2_out, ~Saida[1], Saida[2]);  // OR_Gate
  and and_1 (and_1_out, Saida[1], ~Saida[2]);  // AND_Gate
  J_K_Flip_Flop FJK0 (.J(or_2_out), .K(and_1_out), .clk(CLK), .Q(Saida[0]), .reset(or_3_out));  // open: Qn, preset
  or or_3 (or_3_out, Clear, Iniciar_em_4);

  // Other names for the same wires on the sheet: I4 = Iniciar_em_4; Q0 = Saida[0]; Q1 = Saida[1]; Q2 = Saida[2]
endmodule
