// Logisim project CONTADORES.circ as structural Verilog
module Contador_de_Pulso_Crescente (
  input  Clock,
  input  Limpa,
  output Q3,
  output Q2,
  output Q1,
  output Q0
);

  wire d_ff_1_qn, d_ff_2_qn, d_ff_3_qn, d_ff_4_qn;

  D_Flip_Flop d_ff_1 (.D(d_ff_1_qn), .clk(Clock), .Q(Q3), .Qn(d_ff_1_qn), .reset(Limpa));  // open: preset
  D_Flip_Flop d_ff_2 (.D(d_ff_2_qn), .clk(d_ff_1_qn), .Q(Q2), .Qn(d_ff_2_qn), .reset(Limpa));  // open: preset
  D_Flip_Flop d_ff_3 (.D(d_ff_3_qn), .clk(d_ff_2_qn), .Q(Q1), .Qn(d_ff_3_qn), .reset(Limpa));  // open: preset
  D_Flip_Flop d_ff_4 (.D(d_ff_4_qn), .clk(d_ff_3_qn), .Q(Q0), .Qn(d_ff_4_qn), .reset(Limpa));  // open: preset

  // Notes on the sheet:
  //   Contador de Pulsos (Ripple Counter)  Em ordem crescente
endmodule
