// Logisim project Registradores.circ as structural Verilog: 5 circuits, main circuit main
module main (
  input  Dado_Serial,
  input  Selecao,
  input  [1:0] Controle,
  input  Dado_Serial_dir,
  input  Dado_Serial_esq,
  input  [3:0] Entrada_Direta,
  output [3:0] out_7,
  output [3:0] out_8,
  output [3:0] out_9
);

  wire Clock, demultiplexer_1_out0, demultiplexer_1_out1;

  Clock CLK (.out(Clock));
  Demultiplexer demultiplexer_1 (
    .out0(demultiplexer_1_out0), .out1(demultiplexer_1_out1), .in(Dado_Serial), .sel(Selecao));
  Registrador_de_Deslocamento registrador_de_deslocamento_1 (
    .Dado_Serial(demultiplexer_1_out0), .Clock(Clock), .Q3(out_7[3]), .Q2(out_7[2]), .Q1(out_7[1]),
    .Q0(out_7[0]));
  Registrador_de_Deslocamento_2 registrador_de_deslocamento_2_1 (
    .Dado_serial(demultiplexer_1_out1), .Clock(Clock), .Q3(out_8[3]), .Q2(out_8[2]), .Q1(out_8[1]),
    .Q0(out_8[0]));
  Registrador_de_Deslocamento_com_Carga_Paralela registrador_de_deslocamento_com_carga_paralela_1 (
    .D3(Entrada_Direta[3]), .D2(Entrada_Direta[2]), .D1(Entrada_Direta[1]), .D0(Entrada_Direta[0]),
    .Dado_Serial_dir(Dado_Serial_dir), .C1(Controle[1]), .C0(Controle[0]), .Dado_serial_esq(Dado_Serial_esq),
    .Clock(Clock), .Q3(out_9[3]), .Q2(out_9[2]), .Q1(out_9[1]), .Q0(out_9[0]));

  // Other names for the same wires on the sheet: DSD = Dado_Serial_dir
endmodule

module Registrador_de_Deslocamento (
  input  Dado_Serial,
  input  Clock,
  output Q3,
  output Q2,
  output Q1,
  output Q0
);

  D_Flip_Flop d_ff_1 (.D(Dado_Serial), .clk(Clock), .Q(Q3));  // open: Qn, preset, reset
  D_Flip_Flop d_ff_2 (.D(Q3), .clk(Clock), .Q(Q2));  // open: Qn, preset, reset
  D_Flip_Flop d_ff_3 (.D(Q2), .clk(Clock), .Q(Q1));  // open: Qn, preset, reset
  D_Flip_Flop d_ff_4 (.D(Q1), .clk(Clock), .Q(Q0));  // open: Qn, preset, reset
endmodule

module Registrador_de_Deslocamento_2 (
  input  Dado_serial,
  input  Clock,
  output Q3,
  output Q2,
  output Q1,
  output Q0
);

  D_Flip_Flop d_ff_1 (.D(Q2), .clk(Clock), .Q(Q3));  // open: Qn, preset, reset
  D_Flip_Flop d_ff_2 (.D(Q1), .clk(Clock), .Q(Q2));  // open: Qn, preset, reset
  D_Flip_Flop d_ff_3 (.D(Q0), .clk(Clock), .Q(Q1));  // open: Qn, preset, reset
  D_Flip_Flop d_ff_4 (.D(Dado_serial), .clk(Clock), .Q(Q0));  // open: Qn, preset, reset
endmodule

module Registrador_de_Deslocamento_com_Carga_Paralela (
  input  D3,
  input  D2,
  input  D1,
  input  D0,
  input  Dado_Serial_dir,
  input  C1,
  input  C0,
  input  Dado_serial_esq,
  input  Clock,
  output Q3,
  output Q2,
  output Q1,
  output Q0
);

  wire multiplexer_1_out, multiplexer_2_out, multiplexer_3_out, multiplexer_4_out;

  D_Flip_Flop d_ff_1 (.D(multiplexer_1_out), .clk(Clock), .Q(Q3));  // open: Qn, preset, reset
  Multiplexer #(.select(2)) multiplexer_1 (
    .in0(Q3), .in1(Q2), .in2(Dado_serial_esq), .in3(D3), .out(multiplexer_1_out), .sel({C1, C0}));
  D_Flip_Flop d_ff_2 (.D(multiplexer_2_out), .clk(Clock), .Q(Q2));  // open: Qn, preset, reset
  Multiplexer #(.select(2)) multiplexer_2 (
    .in0(Q2), .in1(Q1), .in2(Q3), .in3(D2), .out(multiplexer_2_out), .sel({C1, C0}));
  Multiplexer #(.select(2)) multiplexer_3 (
    .in0(Q1), .in1(Q0), .in2(Q2), .in3(D1), .out(multiplexer_3_out), .sel({C1, C0}));
  D_Flip_Flop d_ff_3 (.D(multiplexer_3_out), .clk(Clock), .Q(Q1));  // open: Qn, preset, reset
  D_Flip_Flop d_ff_4 (.D(multiplexer_4_out), .clk(Clock), .Q(Q0));  // open: Qn, preset, reset
  Multiplexer #(.select(2)) multiplexer_4 (
    .in0(Q0), .in1(Dado_Serial_dir), .in2(Q1), .in3(D0), .out(multiplexer_4_out), .sel({C1, C0}));
endmodule

module registrador_com_carga_paralela (
  input  D3,
  input  D2,
  input  D1,
  input  D0,
  input  in_5,
  output out_6,
  output out_7,
  output out_8,
  output out_9
);

  wire CLK_out, d_ff_1_q, d_ff_2_q, d_ff_3_q, d_ff_4_q;

  Clock CLK (.out(CLK_out));
  D_Flip_Flop d_ff_1 (.D(D3), .clk(CLK_out), .Q(d_ff_1_q));  // open: Qn, preset, reset
  D_Flip_Flop d_ff_2 (.D(D2), .clk(CLK_out), .Q(d_ff_2_q));  // open: Qn, preset, reset
  assign out_6 = in_5 ? d_ff_1_q : 1'bz;  // Controlled_Buffer controlled_buffer_1
  assign out_7 = in_5 ? d_ff_2_q : 1'bz;  // Controlled_Buffer controlled_buffer_2
  D_Flip_Flop d_ff_3 (.D(D1), .clk(CLK_out), .Q(d_ff_3_q));  // open: Qn, preset, reset
  D_Flip_Flop d_ff_4 (.D(D0), .clk(CLK_out), .Q(d_ff_4_q));  // open: Qn, preset, reset
  assign out_8 = in_5 ? d_ff_3_q : 1'bz;  // Controlled_Buffer controlled_buffer_3
  assign out_9 = in_5 ? d_ff_4_q : 1'bz;  // Controlled_Buffer controlled_buffer_4
endmodule
