// Logisim project carrylookahead - Copia.circ as structural Verilog: 6 circuits, main circuit Carry_lookahead
module MAIN (
  input  [31:0] A,
  input  CONTROLE,
  input  [31:0] B,
  output [31:0] out_4
);

  Circuito circuito_1 (.A(A), .Controle(CONTROLE), .B(B), .SAIDA(out_4));

  // Notes on the sheet:
  //   0 = Soma
  //   1 = Subtração
endmodule

module Circuito (
  input  [31:0] A,
  input  Controle,
  input  [31:0] B,
  output [31:0] SAIDA
);

  wire C4, C8, C12, C16, C20, C24, C28, C32, G0, G00, G1, G2, G3, G11, G22, G33, P0, P00, P1, P2, P3, P11,
       P22, P33;

  LED led_1 (.in(C32));
  CLG_4 clg_4_1 (
    .CLA_4_1_G0(G0), .CLA_4_1_P0(P0), .CLA_4_4_G3(G3), .CLA_4_4_P3(P3), .CLA_4_3_G2(G2), .CLA_4_3_P2(P2),
    .CLA_4_2_G1(G1), .CLA_4_2_P1(P1), .C4(C4), .C16(C16), .C12(C12), .C8(C8));  // open: C0
  CLG_4 clg_4_2 (
    .CLA_4_1_G0(G00), .CLA_4_1_P0(P00), .CLA_4_4_G3(G33), .CLA_4_4_P3(P33), .CLA_4_3_G2(G22),
    .CLA_4_3_P2(P22), .CLA_4_2_G1(G11), .CLA_4_2_P1(P11), .C0(C16), .C4(C20), .C16(C32), .C12(C28), .C8(C24));
  CLA cla_1 (.A(A[3:0]), .B(B[3:0]), .Cin(Controle), .Controle(Controle), .S(SAIDA[3:0]), .Prop(P0), .Gen(G0));
  CLA cla_2 (.A(A[7:4]), .B(B[7:4]), .Cin(C4), .Controle(Controle), .S(SAIDA[7:4]), .Prop(P1), .Gen(G1));
  CLA cla_3 (.A(A[11:8]), .B(B[11:8]), .Cin(C8), .Controle(Controle), .S(SAIDA[11:8]), .Prop(P2), .Gen(G2));
  CLA cla_4 (.A(A[15:12]), .B(B[15:12]), .Cin(C12), .Controle(Controle), .S(SAIDA[15:12]), .Prop(P3), .Gen(G3));
  CLA cla_5 (.A(A[19:16]), .B(B[19:16]), .Cin(C16), .Controle(Controle), .S(SAIDA[19:16]), .Prop(P00), .Gen(G00));
  CLA cla_6 (.A(A[23:20]), .B(B[23:20]), .Cin(C20), .Controle(Controle), .S(SAIDA[23:20]), .Prop(P11), .Gen(G11));
  CLA cla_7 (.A(A[27:24]), .B(B[27:24]), .Cin(C24), .Controle(Controle), .S(SAIDA[27:24]), .Prop(P22), .Gen(G22));
  CLA cla_8 (.A(A[31:28]), .B(B[31:28]), .Cin(C28), .Controle(Controle), .S(SAIDA[31:28]), .Prop(P33), .Gen(G33));
endmodule

module CLA (
  input  [3:0] A,
  input  [3:0] B,
  input  Cin,
  input  Controle,
  output [3:0] S,
  output Prop,
  output Gen
);

  wire B0, B1, B2, B3;

  xor xor_1 (B0, B[0], Controle);
  xor xor_2 (B1, B[1], Controle);
  xor xor_3 (B2, B[2], Controle);
  xor xor_4 (B3, B[3], Controle);
  Carry_lookahead carry_lookahead_1 (
    .A2(A[2]), .B2(B2), .A1(A[1]), .B1(B1), .A0(A[0]), .B0(B0), .A3(A[3]), .B3(B3), .C0(Cin), .S0(S[0]),
    .S1(S[1]), .Prop(Prop), .Gen(Gen), .S2(S[2]), .S3(S[3]));
endmodule

module Carry_lookahead (
  input  A2,
  input  B2,
  input  A1,
  input  B1,
  input  A0,
  input  B0,
  input  A3,
  input  B3,
  input  C0,
  output S0,
  output S1,
  output Prop,
  output Gen,
  output S2,
  output S3
);

  wire and_2_out, and_3_out, and_4_out, and_5_out, and_6_out, and_7_out, and_8_out, and_9_out, and_10_out,
       C1_out, C2_out, C3_out, G0_out, G1_out, G2_out, G3_out, P0_out, P1_out, P2_out, P3_out;

  and and_1 (Prop, P3_out, P2_out, P1_out, P0_out);
  and and_2 (and_2_out, P3_out, P2_out, P1_out, G0_out);
  and and_3 (and_3_out, G2_out, P3_out);
  and and_4 (and_4_out, P3_out, P2_out, G1_out);
  or C4 (Gen, and_3_out, G3_out, and_2_out, and_4_out);
  and G3 (G3_out, A3, B3);
  xor P3 (P3_out, A3, B3);
  and and_5 (and_5_out, G1_out, P2_out);
  xor xor_1 (S3, P3_out, C3_out);
  and and_6 (and_6_out, G0_out, P2_out, P1_out);
  or C3 (C3_out, and_5_out, and_6_out, G2_out, and_7_out);
  and G2 (G2_out, A2, B2);
  and and_7 (and_7_out, P2_out, P1_out, P0_out, C0);
  xor P2 (P2_out, A2, B2);
  and and_8 (and_8_out, P1_out, P0_out, C0);
  xor xor_2 (S2, P2_out, C2_out);
  xor P1 (P1_out, A1, B1);
  and G1 (G1_out, A1, B1);
  and and_9 (and_9_out, P1_out, G0_out);
  or C2 (C2_out, and_8_out, G1_out, and_9_out);
  xor xor_3 (S1, P1_out, C1_out);
  and G0 (G0_out, A0, B0);
  and and_10 (and_10_out, P0_out, C0);
  or C1 (C1_out, G0_out, and_10_out);
  xor P0 (P0_out, A0, B0);
  xor xor_4 (S0, P0_out, C0);

  // Notes on the sheet:
  //   SOMADOR CARRY LOOK-A-HEAD
  //   Generate
  //   G= A x B
  //   Ci+1 = G0+P0.Cin
  //   Propragate
  //   P = A xor B
endmodule

module BGP_8 (
  input  G1,
  input  P1,
  input  G0,
  input  P0,
  input  Ci,
  output Cout,
  output C4
);

  wire and_1_out, and_2_out, and_3_out;

  and and_1 (and_1_out, P0, Ci, P1);
  or or_1 (Cout, G1, and_1_out, and_2_out);
  and and_2 (and_2_out, P1, G0);
  or or_2 (C4, G0, and_3_out);
  and and_3 (and_3_out, P0, Ci);
endmodule

module CLG_4 (
  input  CLA_4_1_G0,
  input  CLA_4_1_P0,
  input  CLA_4_4_G3,
  input  CLA_4_4_P3,
  input  CLA_4_3_G2,
  input  CLA_4_3_P2,
  input  CLA_4_2_G1,
  input  CLA_4_2_P1,
  input  C0,
  output C4,
  output C16,
  output C12,
  output C8
);

  wire and_1_out, and_2_out, and_3_out, and_4_out, and_5_out, and_6_out, and_7_out, and_8_out, and_9_out,
       and_10_out;

  and and_1 (and_1_out, CLA_4_4_P3, CLA_4_3_G2);
  and and_2 (and_2_out, CLA_4_4_P3, CLA_4_3_P2, CLA_4_2_G1);
  or or_1 (C16, CLA_4_4_G3, and_1_out, and_2_out, and_3_out, and_4_out);
  and and_3 (and_3_out, CLA_4_4_P3, CLA_4_3_P2, CLA_4_2_G1, CLA_4_1_G0);
  and and_4 (and_4_out, CLA_4_4_P3, CLA_4_3_P2, CLA_4_2_P1, CLA_4_1_P0, C0);
  and and_5 (and_5_out, CLA_4_3_P2, CLA_4_2_G1);
  or or_2 (C12, CLA_4_3_G2, and_5_out, and_6_out, and_7_out);
  and and_6 (and_6_out, CLA_4_3_P2, CLA_4_2_P1, CLA_4_1_G0);
  and and_7 (and_7_out, CLA_4_3_P2, CLA_4_2_P1, CLA_4_1_P0, C0);
  and and_8 (and_8_out, CLA_4_2_P1, CLA_4_1_G0);
  and and_9 (and_9_out, CLA_4_2_P1, CLA_4_1_P0, C0);
  or or_3 (C8, CLA_4_2_G1, and_8_out, and_9_out);
  and and_10 (and_10_out, CLA_4_1_P0, C0);
  or or_4 (C4, CLA_4_1_G0, and_10_out);
endmodule
