// Logisim project Carry Select RhuanPaiva.circ as structural Verilog: 4 circuits, main circuit main
module main (
  input  Sub,
  input  [31:0] A,
  input  [31:0] B,
  output [31:0] ResultadoFinal,
  output Overflow
);

  wire carry_select_1_cout, carry_select_2_cout, carry_select_3_cout, carry_select_4_cout,
       carry_select_5_cout, carry_select_6_cout, rca4_1_cout;

  RCA4 rca4_1 (
    .a0(A[0]), .b0(B[0]), .Cin(Sub), .a1(A[1]), .Sub(Sub), .b1(B[1]), .a2(A[2]), .b2(B[2]), .a3(A[3]),
    .b3(B[3]), .s0(ResultadoFinal[0]), .s1(ResultadoFinal[1]), .s2(ResultadoFinal[2]),
    .s3(ResultadoFinal[3]), .Cout(rca4_1_cout));  // open: Overflow
  Carry_Select carry_select_1 (
    .A(A[7:4]), .Sub(Sub), .Cin(rca4_1_cout), .B(B[7:4]), .Resultado(ResultadoFinal[7:4]),
    .Cout(carry_select_1_cout));  // open: Overflow
  Carry_Select carry_select_2 (
    .A(A[11:8]), .Sub(Sub), .Cin(carry_select_1_cout), .B(B[11:8]), .Resultado(ResultadoFinal[11:8]),
    .Cout(carry_select_2_cout));  // open: Overflow
  Carry_Select carry_select_3 (
    .A(A[15:12]), .Sub(Sub), .Cin(carry_select_2_cout), .B(B[15:12]), .Resultado(ResultadoFinal[15:12]),
    .Cout(carry_select_3_cout));  // open: Overflow
  Carry_Select carry_select_4 (
    .A(A[19:16]), .Sub(Sub), .Cin(carry_select_3_cout), .B(B[19:16]), .Resultado(ResultadoFinal[19:16]),
    .Cout(carry_select_4_cout));  // open: Overflow
  Carry_Select carry_select_5 (
    .A(A[23:20]), .Sub(Sub), .Cin(carry_select_4_cout), .B(B[23:20]), .Resultado(ResultadoFinal[23:20]),
    .Cout(carry_select_5_cout));  // open: Overflow
  Carry_Select carry_select_6 (
    .A(A[27:24]), .Sub(Sub), .Cin(carry_select_5_cout), .B(B[27:24]), .Resultado(ResultadoFinal[27:24]),
    .Cout(carry_select_6_cout));  // open: Overflow
  Carry_Select carry_select_7 (
    .A(A[31:28]), .Sub(Sub), .Cin(carry_select_6_cout), .B(B[31:28]), .Resultado(ResultadoFinal[31:28]),
    .Overflow(Overflow));  // open: Cout
endmodule

module Carry_Select (
  input  [3:0] A,
  input  Sub,
  input  Cin,
  input  [3:0] B,
  output [3:0] Resultado,
  output Cout,
  output Overflow
);

  wire rca4_1_cout, rca4_1_overflow, rca4_1_s0, rca4_1_s1, rca4_1_s2, rca4_1_s3, rca4_2_cout,
       rca4_2_overflow, rca4_2_s0, rca4_2_s1, rca4_2_s2, rca4_2_s3;

  RCA4 rca4_1 (
    .a0(A[0]), .b0(B[0]), .Cin(1'b0), .a1(A[1]), .Sub(Sub), .b1(B[1]), .a2(A[2]), .b2(B[2]), .a3(A[3]),
    .b3(B[3]), .s0(rca4_1_s0), .s1(rca4_1_s1), .s2(rca4_1_s2), .s3(rca4_1_s3), .Cout(rca4_1_cout),
    .Overflow(rca4_1_overflow));
  RCA4 rca4_2 (
    .a0(A[0]), .b0(B[0]), .Cin(1'b1), .a1(A[1]), .Sub(Sub), .b1(B[1]), .a2(A[2]), .b2(B[2]), .a3(A[3]),
    .b3(B[3]), .s0(rca4_2_s0), .s1(rca4_2_s1), .s2(rca4_2_s2), .s3(rca4_2_s3), .Cout(rca4_2_cout),
    .Overflow(rca4_2_overflow));
  Multiplexer multiplexer_1 (.in0(rca4_1_s1), .in1(rca4_2_s1), .out(Resultado[1]), .sel(Cin));
  Multiplexer multiplexer_2 (.in0(rca4_1_s2), .in1(rca4_2_s2), .out(Resultado[2]), .sel(Cin));
  Multiplexer multiplexer_3 (.in0(rca4_1_cout), .in1(rca4_2_cout), .out(Cout), .sel(Cin));
  Multiplexer multiplexer_4 (.in0(rca4_1_s0), .in1(rca4_2_s0), .out(Resultado[0]), .sel(Cin));
  Multiplexer multiplexer_5 (.in0(rca4_1_s3), .in1(rca4_2_s3), .out(Resultado[3]), .sel(Cin));
  Multiplexer multiplexer_6 (.in0(rca4_1_overflow), .in1(rca4_2_overflow), .out(Overflow), .sel(Cin));
endmodule

module FullAdder (
  input  A,
  input  B,
  input  Sub,
  input  Cin,
  output Cout,
  output S
);

  wire and_1_out, and_2_out, xor_1_out, xor_2_out;

  xor xor_1 (xor_1_out, B, Sub);
  and and_1 (and_1_out, A, xor_1_out);
  xor xor_2 (xor_2_out, A, xor_1_out);
  and and_2 (and_2_out, Cin, xor_2_out);
  xor xor_3 (S, xor_2_out, Cin);
  or or_1 (Cout, and_1_out, and_2_out);
endmodule

module RCA4 (
  input  a0,
  input  b0,
  input  Cin,
  input  a1,
  input  Sub,
  input  b1,
  input  a2,
  input  b2,
  input  a3,
  input  b3,
  output s0,
  output s1,
  output s2,
  output s3,
  output Cout,
  output Overflow
);

  wire fulladder_1_cout, fulladder_2_cout, fulladder_3_cout;

  FullAdder fulladder_1 (.A(a0), .B(b0), .Sub(Sub), .Cin(Cin), .Cout(fulladder_1_cout), .S(s0));
  FullAdder fulladder_2 (.A(a1), .B(b1), .Sub(Sub), .Cin(fulladder_1_cout), .Cout(fulladder_2_cout), .S(s1));
  FullAdder fulladder_3 (.A(a2), .B(b2), .Sub(Sub), .Cin(fulladder_2_cout), .Cout(fulladder_3_cout), .S(s2));
  FullAdder fulladder_4 (.A(a3), .B(b3), .Sub(Sub), .Cin(fulladder_3_cout), .Cout(Cout), .S(s3));
  xor xor_1 (Overflow, fulladder_3_cout, Cout);
endmodule
